# Fritzing sketch ebook flipper (saved by Fritzing 0.9.4)

parts:
  Part1 = Arduino MKR WiFi 1010
  U1 = 60LTR11AIP [part_number=60LTR11AIP]
  U2 = 60LTR11AIP [part_number=60LTR11AIP]

nets:
  N1: Part1.A2, U1.TD
  N2: Part1.A3, U2.pd
  N3: Part1.A4, U2.TD
  N4: Part1.A5, U1.pd
  GND: Part1.GND, U1.GND, U2.GND
  VIN: Part1.VCC, U1.vin, U2.vin

custom parts:
  Arduino MKR WiFi 1010: This is the newest version of the MKR 1000 WIFI, but with an ESP32 module on board made by U-BLOX.
